# Fritzing sketch wifi_fritzing (saved by Fritzing 0.9.3b)
breadboards: 1

parts:
  U2 = ESP8266 WiFi Module [part_number=ESP8266]
  부품1 = Arduino Uno (Rev3)

nets:
  N1: U2.RXD, 부품1.D3_PWM
  VCC: U2.VCC, U2.CH_PD, 부품1.3V3
  GND: U2.GND, 부품1.GND
  N2: U2.TXD, 부품1.D2

custom parts:
  ESP8266 WiFi Module: Generic WiFi Module based on the ESP8266 with onboard PCB antenna and UART communications
